// Logisim project baithuchanhlap1.circ as structural Verilog: 1 circuit, main circuit main
module main (
  input  A,
  input  A_2,
  input  B,
  input  B_2,
  input  C,
  input  D,
  input  A_3,
  input  B_3,
  input  A_4,
  input  Preset_A,
  input  Clear_A,
  input  B_4,
  input  C_2,
  input  Preset_B,
  input  Clear_B,
  output out_16,
  output out_17,
  output C_3,
  output out_19,
  output out_20,
  output D_2,
  output A_output,
  output F,
  output B_output
);

  wire and_1_out, and_2_out, and_3_out, and_4_out, clock_1_out, clock_2_out, nand_1_out, nor_1_out,
       not_1_out, not_2_out, not_3_out, not_4_out, xnor_1_out;

  not not_1 (not_1_out, B);
  not not_2 (not_2_out, A);
  not not_3 (not_3_out, A);
  not not_4 (not_4_out, B);
  and and_1 (and_1_out, A, not_1_out);
  and and_2 (and_2_out, not_2_out, B);
  and and_3 (and_3_out, not_3_out, not_4_out);
  and and_4 (and_4_out, A, B);
  or or_1 (C_3, and_1_out, and_2_out);
  or or_2 (D_2, and_3_out, and_4_out);
  nor nor_1 (nor_1_out, A_3, B_3);
  nand nand_1 (nand_1_out, A_3, C_2);
  xnor xnor_1 (xnor_1_out, B_3, C_2);
  ExactlyOne xor_1 (.out(F), .in0(nor_1_out), .in1(nand_1_out), .in2(xnor_1_out));
  Clock clock_1 (.out(clock_1_out));
  Clock clock_2 (.out(clock_2_out));
  Register #(.width(4), .trigger("falling")) register_1 (
    .D({D, C, B_2, A_2}), .en(1'b1), .Q({out_20, out_19, out_17, out_16}), .clk(clock_1_out));  // open: clr
  D_Flip_Flop d_ff_1 (
    .clk(clock_2_out), .D(A_4), .Q(A_output), .preset(Preset_A), .en(Clear_B), .reset(Clear_A));  // open: Qn
  D_Flip_Flop d_ff_2 (
    .clk(clock_2_out), .D(B_4), .Q(B_output), .preset(Preset_B), .en(Clear_B), .reset(Clear_B));  // open: Qn
  // also tied to GND on the sheet: Clear_B

  // Notes on the sheet:
  //   clock
  //   clock
  //   A_output
  //   B_output
  //   C_output
  //   D_output
endmodule
