// Logisim project 3.2 thuchanh lap2.circ as structural Verilog: 1 circuit, main circuit main
module main (
  input  [1:0] in_1,
  input  [7:0] \Ngõ_vào_dữ_liệu ,
  input  in_3,
  input  [7:0] \Ngõ_ra 
);

  wire clock_1_out, decoder_1_out0, decoder_1_out1, decoder_1_out2, decoder_1_out3;
  wire [7:0] register_1_q, register_2_q, register_3_q, register_4_q;

  Decoder #(.select(2)) decoder_1 (
    .out0(decoder_1_out0), .out1(decoder_1_out1), .out2(decoder_1_out2), .out3(decoder_1_out3), .sel(in_1),
    .en(in_3));
  Clock clock_1 (.out(clock_1_out));
  Register register_1 (.D(\Ngõ_vào_dữ_liệu ), .en(decoder_1_out0), .Q(register_1_q), .clk(clock_1_out));  // open: clr
  Register register_2 (.D(\Ngõ_vào_dữ_liệu ), .en(decoder_1_out1), .Q(register_2_q), .clk(clock_1_out));  // open: clr
  Register register_3 (.D(\Ngõ_vào_dữ_liệu ), .en(decoder_1_out2), .Q(register_3_q), .clk(clock_1_out));  // open: clr
  Register register_4 (.D(\Ngõ_vào_dữ_liệu ), .en(decoder_1_out3), .Q(register_4_q), .clk(clock_1_out));  // open: clr
  Multiplexer #(.select(2), .width(8)) multiplexer_1 (
    .in0(register_4_q), .in1(register_1_q), .in2(register_2_q), .in3(register_3_q), .out(\Ngõ_ra ), .sel(in_1));  // open: en

  // Notes on the sheet:
  //   A 
  //   clock 
  //   output 
endmodule
