// Logisim project bài 3.1 thuchanh2.circ as structural Verilog: 1 circuit, main circuit main
module main (
  input  [2:0] in_1,
  input  [7:0] in_2,
  input  [7:0] in_3,
  output [7:0] \Ngõ_ra 
);

  wire [7:0] adder_1_out, adder_2_out, and_1_out, or_1_out, subtractor_1_out, subtractor_2_out, xnor_1_out,
       xor_1_out;

  Adder adder_1 (.a(in_2), .b(in_3), .out(adder_1_out));  // open: cin, cout
  Adder adder_2 (.a(in_2), .b(8'h1), .out(adder_2_out));  // open: cin, cout
  Subtractor subtractor_1 (.a(in_2), .b(in_3), .out(subtractor_1_out));  // open: bin, bout
  Subtractor subtractor_2 (.a(in_2), .b(8'h1), .out(subtractor_2_out));  // open: bin, bout
  assign and_1_out = in_2 & in_3;  // AND_Gate and_1, 8 bits wide
  assign or_1_out = in_2 | in_3;  // OR_Gate or_1, 8 bits wide
  assign xor_1_out = in_2 ^ in_3;  // XOR_Gate xor_1, 8 bits wide
  assign xnor_1_out = ~(in_2 ^ in_3);  // XNOR_Gate xnor_1, 8 bits wide
  Multiplexer #(.select(3), .width(8)) multiplexer_1 (
    .in0(adder_1_out), .in1(adder_2_out), .in2(subtractor_1_out), .in3(subtractor_2_out), .in4(and_1_out),
    .in5(or_1_out), .in6(xor_1_out), .in7(xnor_1_out), .out(\Ngõ_ra ), .sel(in_1));  // open: en

  // Notes on the sheet:
  //   B
  //   Ngõ vào dữ liệu 
  //   A
  //   Ngõ vào điều khiển 
  //   output
endmodule
